// Logisim project data_path.circ as structural Verilog: 1 circuit, main circuit main
module main (
  input  [31:0] in_1,
  input  [31:0] in_2,
  input  [31:0] in_3,
  input  [31:0] in_4,
  input  [31:0] in_5,
  input  [31:0] in_6,
  input  [31:0] in_7,
  input  [31:0] in_8,
  input  [31:0] in_9,
  input  [31:0] in_10,
  input  [31:0] in_11,
  input  [31:0] in_12,
  input  [31:0] in_13,
  input  [31:0] in_14,
  input  [31:0] in_15,
  input  [31:0] in_16,
  input  [31:0] in_17,
  input  [31:0] in_18,
  input  [31:0] in_19,
  input  [31:0] in_20,
  input  [31:0] in_21,
  input  [31:0] in_22,
  input  [31:0] in_23,
  input  [31:0] in_24,
  input  [31:0] in_25,
  input  [31:0] in_26,
  input  [31:0] in_27,
  input  [31:0] in_28,
  input  [31:0] in_29,
  input  [31:0] in_30,
  input  [31:0] in_31,
  input  [31:0] in_32,
  input  [31:0] in_33,
  output out_34,
  output out_35
);

  wire clock, Extop, jalr, less_flag_signed, less_flag_unsigned, mem_to_reg, Memory_Write, Output_Enable,
       pc_src, RegWrite, SSET, Zero_flag;
  wire [1:0] ALUsrc;
  wire [4:0] Imm16, ImmL, multiplexer_1_out, RS1;
  wire [7:0] ALU_Op;
  wire [10:0] Funct;
  wire [15:0] Imm_16, instruction;
  wire [19:0] Pc, pc_inc, pc_next;
  wire [31:0] ALU_Result, ALU_result_t, bit_extender_1_out, bit_extender_2_out, bit_extender_3_out,
       bit_extender_4_out, BusA, BusB, main_2_p5, multiplexer_2_out, multiplexer_4_out, multiplexer_5_out,
       Write_Data;

  instruction_mem_main main_1 (.in_1(Pc), .out_2({Funct, Imm16, instruction[15:11], ImmL, instruction[5:0]}));
  // data_mem_main main_2: pin names not known; wires that end beside it: ALU_Result, clock, Output_Enable, Memory_Write, main_2_p5
  Multiplexer #(.width(5), .enable("false")) multiplexer_1 (.in0(RS1), .in1(ImmL), .out(multiplexer_1_out), .sel(SSET));
  Multiplexer #(.width(32), .enable("false")) multiplexer_2 (
    .in0(ALU_result_t), .in1(main_2_p5), .out(multiplexer_2_out), .sel(mem_to_reg));
  assign bit_extender_1_out = {{12{1'b0}}, pc_inc};  // Bit_Extender bit_extender_1
  Clock clock_1 (.out(clock));
  Multiplexer #(.width(32), .enable("false")) multiplexer_3 (
    .in0(multiplexer_2_out), .in1(bit_extender_1_out), .out(Write_Data), .sel(jalr));
  assign bit_extender_2_out = {{16{1'b0}}, {Funct, Imm16}};  // Bit_Extender bit_extender_2
  assign bit_extender_3_out = {{16{Funct[10]}}, {Funct, Imm16}};  // Bit_Extender bit_extender_3
  assign bit_extender_4_out = {{16{Funct[10]}}, {Funct, ImmL}};  // Bit_Extender bit_extender_4
  Multiplexer #(.width(32), .enable("false")) multiplexer_4 (
    .in0(bit_extender_2_out), .in1(bit_extender_3_out), .out(multiplexer_4_out), .sel(Extop));
  Reg_file reg_file_1 (
    .out_7(in_1), .out_19(BusA), .out_28(BusB), .RW(ImmL), .Reg_Write(RegWrite), .DATA_IN(Write_Data),
    .clock(clock), .BusB(Imm16), .BusA(multiplexer_1_out), .out_9(in_4), .out_11(in_9), .out_14(in_13),
    .out_15(in_17), .out_16(in_19), .out_17(in_23), .out_18(in_21), .out_20(in_27), .out_21(in_25),
    .out_22(in_31), .out_23(in_29), .out_24(in_3), .out_25(in_33), .out_26(in_7), .out_29(in_12),
    .out_27(in_5), .out_30(in_10), .out_32(in_16), .out_31(in_14), .out_34(in_20), .out_33(in_18),
    .out_37(in_28), .out_39(in_32), .out_36(in_22), .out_35(in_24), .out_38(in_26), .out_40(in_30),
    .out_8(in_2), .out_10(in_6), .out_12(in_11), .out_13(in_15));
  Multiplexer #(.select(2), .width(32), .enable("false")) multiplexer_5 (
    .in0(BusB), .in1(multiplexer_4_out), .in2(bit_extender_4_out), .out(multiplexer_5_out), .sel(ALUsrc));  // open: in3
  pc_circut_main main_3 (
    .pc_src(pc_src), .next_pc(pc_next), .out_9(pc_inc), .Lower5(ImmL), .upper11(Funct), .IMM16(Imm_16),
    .in_3(clock), .RS1(BusA), .jalr(jalr));  // open: out_10
  ALU_Full alu_full_1 (
    .OverFlow(out_34), .AInvert(ALU_Op[7]), .CarryIn(ALU_Op[6]), .in_2(BusA), .in_4(multiplexer_5_out),
    .Operation(ALU_Op[5:4]), .BInvert(ALU_Op[6]), .select_Alu(ALU_Op[3:0]),
    .less_flag_signed(less_flag_unsigned), .out_11(less_flag_signed), .out_9(ALU_Result), .in_5(BusA),
    .out_14(out_35), .zreo_flag(Zero_flag));

  assign in_8 = in_7;

  // Other names for the same wires on the sheet: instruction (some bits) = {Funct, Imm16, ImmL}; Rd[4:0] = ImmL;
  //   Imm16[15:5] = Funct; ImmU[10:0] = Funct; OP[5:0] = instruction[5:0]; Rs1_t[4:0] = instruction[15:11];
  //   Rs2[4:0] = Imm16; R0[31:0] = in_1; R1[31:0] = in_2; R2[31:0] = in_4; R3[31:0] = in_6; R4[31:0] = in_9;
  //   R5[31:0] = in_11; R6[31:0] = in_13; R7[31:0] = in_15; R8[31:0] = in_17; R9[31:0] = in_19; R10[31:0] = in_21;
  //   R11[31:0] = in_23; R12[31:0] = in_25; R13[31:0] = in_27; R14[31:0] = in_29; R15[31:0] = in_31;
  //   R16[31:0] = in_33; R17[31:0] = in_3; R18[31:0] = in_5; R19[31:0] = in_7; R20[31:0] = in_10; R21[31:0] = in_12;
  //   R22[31:0] = in_14; R23[31:0] = in_16; R24[31:0] = in_18; R25[31:0] = in_20; R26[31:0] = in_22;
  //   R27[31:0] = in_24; R28[31:0] = in_26; R29[31:0] = in_28; R30[31:0] = in_30; R31[31:0] = in_32

  // Notes on the sheet:
  //   Registers
  //   Instruction_Memory
  //   Data_Memory
  //   Decoding_Instruction
  //   signal
  //   old_Rd_for_sset_instruction
  //   ALU
endmodule
